# Fritzing sketch fan-speed-controller (saved by Fritzing 0.9.9b)
circuit board: 4.18664cm x 4.65408cm
breadboards: 1

parts:
  7805 = Voltage Regulator [package=to220-igo]
  10kΩ = Resistor [tolerance=±5% resistance=1k power=0.25 package=THT]
  Terminal_Block = Camdenboss CTB0158-7 [part_number=CTB0158-7 package=THT]
  1kΩ = Resistor [tolerance=±5% resistance=1k power=0.25 package=THT]
  100nf = Ceramic Capacitor [capacitance=100nF voltage=35V package="100 mil [THT, multilayer]"]
  330nf = Ceramic Capacitor [capacitance=0pF voltage=35V package="100 mil [THT, multilayer]"]
  20kΩ = Resistor [tolerance=±5% resistance=10k power=0.25 package=THT]
  220Ω = Resistor [tolerance=±5% resistance=220 power=0.25 package=THT]
  N-FET = Basic FET N-Channel [package="TO220 [THT]"]
  47nf = Ceramic Capacitor [capacitance=100n voltage=35V package="200 mil [THT, multilayer]"]
  10kΩ_2 = Resistor [tolerance=±5% resistance=10k power=0.25 package=THT]
  Z5V = Zener Diode [part_number=1N4732A breakdown_voltage=3.6V package="300 mil [THT]"]
  10kΩ_3 = Resistor [tolerance=±5% resistance=10k power=0.25 package=THT]
  Z5V_2 = Zener Diode [part_number=1N4732A breakdown_voltage=3.6V package="300 mil [THT]"]
  10kΩ_4 = Resistor [tolerance=±5% resistance=10k power=0.25 package=THT]
  Z5V_3 = Zener Diode [part_number=1N4732A breakdown_voltage=3.6V package="300 mil [THT]"]
  10kΩ_5 = Resistor [tolerance=±5% resistance=10k power=0.25 package=THT]
  Z5V_4 = Zener Diode [part_number=1N4732A breakdown_voltage=3.6V package="300 mil [THT]"]
  20kΩ_2 = Resistor [tolerance=±5% resistance=10k power=0.25 package=THT]
  20kΩ_3 = Resistor [tolerance=±5% resistance=10k power=0.25 package=THT]
  20kΩ_4 = Resistor [tolerance=±5% resistance=10k power=0.25 package=THT]
  20kΩ_5 = Resistor [tolerance=±5% resistance=10k power=0.25 package=THT]
  ATTINY85 = attiny85 [package=dip]

nets:
  N1: 7805.GND, Terminal_Block.pin6, 100nf.0, 330nf.0, 20kΩ.Pin_1, 47nf.0, Z5V.anode, Z5V_2.anode, Z5V_3.anode, Z5V_4.anode, 20kΩ_2.Pin_0, 20kΩ_3.Pin_0, 20kΩ_4.Pin_0, 20kΩ_5.Pin_0, ATTINY85.Pin_4
  N2: 7805.IN, Terminal_Block.pin1, 330nf.1, N-FET.drain
  N3: 7805.OUT, 10kΩ.Pin_1, 100nf.1, ATTINY85.Pin_8
  N4: 10kΩ.Pin_0, ATTINY85.Pin_1
  N5: Terminal_Block.pin2, 10kΩ_2.Pin_0
  N6: Terminal_Block.pin3, 10kΩ_3.Pin_0
  N7: Terminal_Block.pin4, 10kΩ_4.Pin_0
  N8: Terminal_Block.pin5, 10kΩ_5.Pin_0
  N9: Terminal_Block.pin7, 220Ω.Pin_1, 47nf.1
  N10: 1kΩ.Pin_0, 20kΩ.Pin_0, ATTINY85.Pin_3
  N11: 1kΩ.Pin_1, N-FET.gate
  N12: 220Ω.Pin_0, N-FET.source
  N13: 10kΩ_2.Pin_1, Z5V.cathode, 20kΩ_2.Pin_1, ATTINY85.Pin_7
  N14: 10kΩ_3.Pin_1, Z5V_2.cathode, 20kΩ_3.Pin_1, ATTINY85.Pin_6
  N15: 10kΩ_4.Pin_1, Z5V_3.cathode, 20kΩ_4.Pin_1, ATTINY85.Pin_5
  N16: 10kΩ_5.Pin_1, Z5V_4.cathode, 20kΩ_5.Pin_1, ATTINY85.Pin_2

notes:
  12V
  GND
  OUT
  SW1
  SW2
  SW3
  SW4
  Fan Speed Controller v5.0
  ©2022 That Ain't Working
